// Logisim project not gate.circ as structural Verilog: 1 circuit, main circuit main
module main (
  input  in_1,
  input  in_2,
  output out_3,
  output out_4
);

  not not_1 (out_3, in_1);
  not not_2 (out_4, in_2);

  // Notes on the sheet:
  //   not gate for 0
  //   not gate for 1
endmodule
