// Logisim project or gate.circ as structural Verilog: 1 circuit, main circuit main
module main (
  input  in_1,
  input  in_2,
  input  in_3,
  input  in_4,
  input  in_5,
  input  in_6,
  input  in_7,
  input  in_8,
  output out_9,
  output out_10,
  output out_11,
  output out_12
);

  or or_1 (out_10, in_2, in_4);
  or or_2 (out_11, in_5, in_7);
  or or_3 (out_9, in_1, in_3);
  or or_4 (out_12, in_6, in_8);

  // Notes on the sheet:
  //   or gate for 0,0
  //   or gate for 0,1
  //   or gate for 1,0
  //   or gate for 1,1
endmodule
